# Fritzing sketch ADC firstRD (saved by Fritzing 0.9.4)
circuit board: 8.46667cm x 5.64444cm
breadboards: 1

parts:
  Clock = ZS-042 RTC Module
  Arduino_Nano = Arduino Nano (Rev3.0) (ICSP)
  DSD_TECH_SH-HC-08_Bluetooth_4_0_BLE1 = Bluetooth HC-05 Macho
  Relay = RELAY [package=relay-g5q]
  STEP_DOWN = RioRand LM2596  # not connected

nets:
  GND: Clock.GND, Arduino_Nano.GND, DSD_TECH_SH-HC-08_Bluetooth_4_0_BLE1.GND
  VCC: Clock.VCC, Arduino_Nano.3V3, DSD_TECH_SH-HC-08_Bluetooth_4_0_BLE1.VCC
  N1: Clock.SDA, Arduino_Nano.A4
  N2: Clock.SCL, Arduino_Nano.A5
  N3: Arduino_Nano.D10, DSD_TECH_SH-HC-08_Bluetooth_4_0_BLE1.TXD
  N4: Arduino_Nano.D11/MOSI, DSD_TECH_SH-HC-08_Bluetooth_4_0_BLE1.RXD
  N5: Arduino_Nano.5V, Relay.MAIN
