# Fritzing sketch BLE (saved by Fritzing 0.9.3b)
circuit board: 8.46667cm x 5.64444cm
breadboards: 1

parts:
  NANO = Arduino Nano (Rev3.0)
  DSD_TECH_SH-HC-08_Bluetooth_4_0_BLE = Bluetooth HC-05 Macho
  RELAY = RELAY [package=relay-g5q]
  OUT = Camdenboss CTB0158-4 [part_number=CTB0158-4 package=THT]

nets:
  GND: NANO.GND, DSD_TECH_SH-HC-08_Bluetooth_4_0_BLE.GND, RELAY.COIL1, OUT.pin1
  N1: NANO.D8, RELAY.COIL2
  N2: NANO.D10, DSD_TECH_SH-HC-08_Bluetooth_4_0_BLE.TXD
  N3: NANO.D11/MOSI, DSD_TECH_SH-HC-08_Bluetooth_4_0_BLE.RXD
  VIN: NANO.VIN, DSD_TECH_SH-HC-08_Bluetooth_4_0_BLE.VCC, OUT.pin2
  N4: RELAY.MAIN, OUT.pin3
  N5: RELAY.NO, OUT.pin4

// code stored in the sketch: Bluetooth.ino
#include <SoftwareSerial.h>
#include "outgoingCommands.h"

#define LED_PIN 5
#define txPin 11
#define rxPin 10

SoftwareSerial adc(rxPin, txPin);
int isLightOn = 0;


# pragma mark - function prototypes

void processData2();

# pragma mark - main arduino methods

void setup() {
    pinMode(rxPin, INPUT);
    pinMode(txPin, OUTPUT);
    pinMode(LED_PIN, OUTPUT);
    Serial.begin(9600);
    adc.begin(9600);
}

void loop() {
    processData2();
}

# pragma mark - helper methods

void processData2() {
    if (adc.available()) {
        char data = adc.read();
        Serial.println(data);
        if (data == 'a') {
            isLightOn = !isLightOn;
            if (isLightOn == 0) {
                adc.print(offCommand);
                digitalWrite(LED_PIN, LOW);
            } else {
                adc.print(onCommand);
                digitalWrite(LED_PIN, HIGH);
            }
        }
    }
}

// code stored in the sketch: outgoingCommands.h.ino
#define onCommand "ON"
#define offCommand "OFF"
